# Fritzing sketch APPLE HOMEBRIDGE – TEMPERATURE & HUMIDITY LEVEL (saved by Fritzing 0.9.3b)
breadboards: 1

parts:
  U1 = ESP8266 WiFi Module [part_number=ESP8266]
  DHT1 = DHT11 Humitidy and Temperature Sensor
  Part1 = FTDI Basic Programmer

nets:
  N1: U1.RXD, Part1.TXO
  VCC: U1.VCC, U1.CH_PD, DHT1.VDD, Part1.POWER
  N2: U1.GPIO_0, DHT1.DATA
  GND: U1.GND, DHT1.GND, Part1.GND
  N3: U1.TXD, Part1.RXI

custom parts:
  ESP8266 WiFi Module: Generic WiFi Module based on the ESP8266 with onboard PCB antenna and UART communications
  DHT11 Humitidy and Temperature Sensor: DHT11 Humidity and Temperature Sensor
